// Logisim project cpu.circ as structural Verilog: 3 circuits, main circuit main
module main (
  input  [31:0] INSTRUCTION,
  input  CLOCK,
  output [31:0] PROGRAM_COUNTER,
  output [31:0] ra,
  output [31:0] sp,
  output [31:0] t0,
  output [31:0] t1,
  output [31:0] t2,
  output [31:0] s0,
  output [31:0] s1,
  output [31:0] a0
);

  wire DMEM_p1, DMEM_p6, DMEM_p8;
  wire [31:0] alu, DMEM_p10, immediate_generator_1_p2, multiplexer_1_out, multiplexer_2_out,
       multiplexer_3_out, multiplexer_4_out, pc_plus_4, RegFile_read_data_1, RegFile_read_data_2,
       register_1_q;

  Adder #(.width(32)) adder_1 (.a(PROGRAM_COUNTER), .b(32'h4), .out(pc_plus_4));  // open: cin, cout
  Multiplexer #(.width(32), .enable("false")) multiplexer_1 (
    .in0(pc_plus_4), .in1(alu), .out(multiplexer_1_out), .sel(1'b0));
  Register #(.width(32)) PC (.D(multiplexer_1_out), .clk(CLOCK), .Q(PROGRAM_COUNTER));  // open: en, clr
  Register #(.width(32)) register_1 (.D(INSTRUCTION), .en(1'b1), .clk(CLOCK), .Q(register_1_q));  // open: clr
  // immediate_generator immediate_generator_1: pin names not known; wires that end beside it: register_1_q[31:7], immediate_generator_1_p2
  regfile_main RegFile (
    .rs2(register_1_q[24:20]), .rd(register_1_q[11:7]), .Read_Data_1(RegFile_read_data_1),
    .Read_Data_2(RegFile_read_data_2), .ra(ra), .sp(sp), .t0(t0), .t1(t1), .t2(t2), .s0(s0), .s1(s1),
    .a0(a0), .rs1(register_1_q[19:15]), .Write_Data(multiplexer_4_out), .RegWEn(1'b1), .clk(CLOCK));
  Multiplexer #(.width(32), .enable("false")) multiplexer_2 (
    .in0(RegFile_read_data_1), .in1(PROGRAM_COUNTER), .out(multiplexer_2_out), .sel(1'b0));
  Multiplexer #(.width(32), .enable("false")) multiplexer_3 (
    .in0(RegFile_read_data_2), .in1(immediate_generator_1_p2), .out(multiplexer_3_out), .sel(1'b1));
  alu Arithmetic_Logic_Unit (.B(multiplexer_3_out), .Result(alu), .A(multiplexer_2_out), .ALUSel(4'b0000));
  // mem_main DMEM: pin names not known; wires that end beside it: DMEM_p1, alu, RegFile_read_data_2, DMEM_p1, CLOCK, DMEM_p6, DMEM_p6, DMEM_p8, 1'b0, DMEM_p10
  Multiplexer #(.select(2), .width(32), .enable("false")) multiplexer_4 (
    .in0(pc_plus_4), .in1(alu), .in2(DMEM_p10), .out(multiplexer_4_out));  // open: in3, sel

  // Other names for the same wires on the sheet: clk = CLOCK

  // Notes on the sheet:
  //   Output
  //   IMEM (do **NOT** move this)
  //   Inputs
  //   Inputs/Outputs for testing. Do **NOT** move these.
endmodule

module control_module (
  input  [31:0] Instruction_32,
  output BrEq,
  output BrLt,
  output PCSel,
  output ImmSel,
  output BrUn,
  output ASel,
  output BSel,
  output ALUSel,
  output MemRW,
  output RegWEn,
  output WBSel
);
endmodule

module immediate_generator (
  input  [2:0] ImmSel,
  input  [24:0] imm,
  output [31:0] immOut
);

  wire [4:0] undriven;
  wire [6:0] undriven_2;

  Multiplexer #(.select(3), .width(32), .enable("false")) multiplexer_1 (
    .out(immOut), .sel(ImmSel));  // open: in0, in1, in2, in3, in4, in5, in6, in7
  Bit_Extender #(.in_width(12), .out_width(32), .\type ("zero")) bit_extender_1 (.in({undriven_2, undriven}));  // open: out

  // Other names for the same wires on the sheet: immIn[24:0] = imm
endmodule
